# Fritzing sketch Plant Waterer (saved by Fritzing 0.9.3b)
breadboards: 2

parts:
  S1 = Momentary Switch [package=ksa_sealed_tac_switch]
  OLED1 = OLED 128x64 I2C Monochrome Display  # not connected
  DHT1 = DHT22 Humidity and Temperature Sensor
  Mod1 = Raspberry Pi Pico
  Part1 = Adafruit ADS1115 16Bit I2C ADC [part_number="Adafruit #1085"]  # not connected
  R1 = Resistor [tolerance=±5% resistance=220 package="2010 [SMD]"]
  R2 = Resistor [tolerance=±5% resistance=220 package="2010 [SMD]"]
  Capacitive_Soil_Moisture_Sensor1 = DFRobot Capacitive Soil Moisture Sensor V1.0 [part_number=SEN0193]
  J1 = female pin header, 5 pins [form="♀ (female)"]
  J2 = female pin header, 3 pins [form="♀ (female)"]
  J3 = female pin header, 5 pins [form="♀ (female)"]
  J4 = female pin header, 4 pins [form="♀ (female)"]
  J5 = female pin header, 3 pins [form="♀ (female)"]
  J6 = female pin header, 4 pins [form="♀ (female)"]
  Capacitive_Soil_Moisture_Sensor2 = DFRobot Capacitive Soil Moisture Sensor V1.0 [part_number=SEN0193]
  Capacitive_Soil_Moisture_Sensor3 = DFRobot Capacitive Soil Moisture Sensor V1.0 [part_number=SEN0193]
  Capacitive_Soil_Moisture_Sensor4 = DFRobot Capacitive Soil Moisture Sensor V1.0 [part_number=SEN0193]

nets:
  N1: S1.1, S1.2, DHT1.GND, Mod1.pin_3, Mod1.pin_5, Mod1.pin_8, Mod1.pin_13, Mod1.pin_18, Mod1.pin_23, Mod1.pin_28, Mod1.pin_33, Mod1.pin_38, Mod1.pin_42, J1.pin1, J1.pin3, J2.pin3, J3.pin2, J3.pin5, J5.pin3, J6.pin4
  N2: S1.3, S1.4
  N3: DHT1.DATA, J5.pin1
  N4: DHT1.NULL, Mod1.pin_4, J1.pin2, J5.pin2
  N5: Mod1.pin_1, R2.Pin_0, J1.pin5, J3.pin4, J6.pin1
  N6: Mod1.pin_2, R1.Pin_0, R1.Pin_1, J1.pin4, J3.pin3, J6.pin2
  N7: Mod1.pin_36, J2.pin1
  N8: Mod1.pin_37, J2.pin2
  N9: Capacitive_Soil_Moisture_Sensor1.A, J4.pin1
  N10: J4.pin2, Capacitive_Soil_Moisture_Sensor2.A
  N11: J4.pin3, Capacitive_Soil_Moisture_Sensor3.A
  N12: J4.pin4, Capacitive_Soil_Moisture_Sensor4.A

notes:
  Ground Wire Nut
  3.3v Wire Nut

custom parts:
  Raspberry Pi Pico: Raspberry Pi Pico. Based around the RP2040 microcontroller the Pico is a low cost microcontroller device bringing Raspberry Pi quality, cost, and easy of use to the microcontroller space. Jan 2021, Split part in to two versions: tht (this one) and SMD. This one will drill holes for a .1 in header in pcb to allow plugging in the module as well as providing pads to solder the module to the top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
  Adafruit ADS1115 16Bit I2C ADC: For microcontrollers without an analog-to-digital converter or when you want a higher-precision ADC, the ADS1115 provides 16-bit precision at 860 samples/second over I2C. The chip can be configured as 4 single-ended input channels, or two differential channels. As a nice bonus, it even includes a programmable gain amplifier, up to x16, to help boost up smaller single/differential signals to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
  DFRobot Capacitive Soil Moisture Sensor V1.0: DFRobot Capacitive Soil Moisture Sensor V1.0 This product measures soil moisture levels by capacitive sensing, rather than resistive sensing like other types of moisture sensor. It is made of a corrosion resistant material giving it a long service life. Insert it into soil and impress your friends with the real-time soil moisture data! The product includes an on-board voltage regulator which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
